# Fritzing sketch main-board (saved by Fritzing 0.9.4)
circuit board: 10.6cm x 15cm
circuit board: 10.6cm x 15cm
breadboards: 1

parts:
  MAX31855 = Adafruit Thermocouple Amplifier MAX31855 [part_number="Adafruit #269"]  # not connected
  H1 = double row female pin header, 40 pins [form="♀ (female)"]
  TRS2 = Audio Jack (TRS) 3.5mm [package="4Ucon 08780 [THT]"]  # not connected
  TRS3 = Audio Jack (TRS) 3.5mm [package="4Ucon 08780 [THT]"]  # not connected
  ADS1115 = Adafruit ADS1115 16Bit I2C ADC [part_number="Adafruit #1085"]
  TRS4 = Audio Jack (TRS) 3.5mm [package="4Ucon 08780 [THT]"]  # not connected
  PCA9685 = 16-Channel 12-bit PWM Servo Driver - I2C [part_number=815]  # not connected
  BSS138 = Adafruit 4-channel I2C-safe Bi-directional Logic Level Converter [part_number="Adafruit #757"]  # not connected
  Mod1 = Raspberry Pi 4B  # not connected
  J1 = female pin header, 6 pins [form="♀ (female)"]
  J2 = female pin header, 6 pins [form="♀ (female)"]
  J3 = female pin header, 6 pins [form="♀ (female)"]
  J4 = female pin header, 6 pins [form="♀ (female)"]
  J5 = female pin header, 10 pins [form="♀ (female)"]
  J6 = female pin header, 10 pins [form="♀ (female)"]
  J8 = female pin header, 2 pins [form="♀ (female)"]
  J9 = female pin header, 2 pins [form="♀ (female)"]
  J10 = female pin header, 2 pins [form="♀ (female)"]  # not connected
  J11 = female pin header, 2 pins [form="♀ (female)"]
  J15 = female pin header, 2 pins [form="♀ (female)"]
  J16 = Screw terminal - 2 pins [package=THT]
  J17 = Screw terminal - 2 pins [package=THT]
  R1 = Resistor [tolerance=±5% resistance=220 package=THT]
  ADS1115_2 = Adafruit ADS1115 16Bit I2C ADC [part_number="Adafruit #1085"]  # not connected
  LED2 = LED - 3mm [color="Red (633nm)" package="3 mm [THT]"]
  LED1 = LED - 3mm [color="Blue (505nm)" package="3 mm [THT]"]
  TRS5 = Audio Jack (TRS) 3.5mm [package="4Ucon 08780 [THT]"]  # not connected
  J19 = female pin header, 2 pins [form="♀ (female)"]
  TRS6 = Audio Jack (TRS) 3.5mm [package="4Ucon 08780 [THT]"]  # not connected
  J21 = female pin header, 2 pins [form="♀ (female)"]
  J22 = female pin header, 2 pins [form="♀ (female)"]
  TRS7 = Audio Jack (TRS) 3.5mm [package="4Ucon 08780 [THT]"]  # not connected
  J23 = female pin header, 2 pins [form="♀ (female)"]
  J24 = female pin header, 2 pins [form="♀ (female)"]
  J26 = female pin header, 1 pin [form="♀ (female)"]
  J27 = female pin header, 1 pin [form="♀ (female)"]
  J28 = female pin header, 1 pin [form="♀ (female)"]
  J29 = female pin header, 1 pin [form="♀ (female)"]  # not connected
  J30 = female pin header, 1 pin [form="♀ (female)"]
  J31 = female pin header, 1 pin [form="♀ (female)"]
  J33 = female pin header, 6 pins [form="♀ (female)"]
  JACK2 = 2.1mm DC Barrel Jack
  J34 = Screw terminal - 2 pins [package=THT]
  J14 = female pin header, 1 pin [form="♀ (female)"]
  J20 = female pin header, 1 pin [form="♀ (female)"]

nets:
  N1: H1.pin1, J2.pin6, J4.pin3, J26.pin1
  N2: H1.pin6, J4.pin5
  N3: H1.pin9, J4.pin6
  N4: H1.pin10, J4.pin4
  N5: H1.pin12, J2.pin1, J4.pin1, J20.pin1
  N6: H1.pin16, J28.pin1
  N7: H1.pin18, J2.pin2, J19.pin2
  N8: H1.pin19, J2.pin3, J19.pin1
  N9: H1.pin21, J3.pin1, J6.pin1, J15.pin1
  N10: H1.pin29, LED2.cathode
  N11: H1.pin30, R1.Pin_0
  N12: H1.pin31, J11.pin1, LED1.cathode
  N13: ADS1115.SDA, J21.pin1, J23.pin1
  N14: ADS1115.SCL, J21.pin2, J23.pin2
  N15: J1.pin3, J5.pin3
  N16: J1.pin4, J5.pin4
  N17: J3.pin2, J6.pin3
  N18: J3.pin3, J6.pin4
  N19: J3.pin6, J6.pin2, J27.pin1
  N20: J5.pin1, J5.pin5, J8.pin2, J22.pin1, J24.pin1, J33.pin5
  N21: J5.pin2, J30.pin1, J31.pin1, J33.pin1
  N22: J5.pin8, J9.pin1
  N23: J6.pin7, J14.pin1
  N24: J16.pin1, JACK2.center
  N25: J16.pin2, JACK2.switch, JACK2.sleeve
  N26: J17.pin1, J34.pin1
  N27: J17.pin2, J34.pin2
  N28: R1.Pin_1, LED2.anode, LED1.anode

notes:
  ADS1115 (5v)
  ADS1115 (3v)
  5V
  GND
  SCL
  SDA
  A0
  3V
  A1
  BSS138
  B1
  B0
  CS
  CLK
  D0
  MAX31855
  R+
  B-
  PWM
  +
  -
  #17
  #4
  #27
  #22
  MISO
  MOSI
  #5
  EED
  #13
  #19
  #6
  #26
  CE1
  EEC
  #24
  #23
  CE0
  #20
  #21
  RXD
  #16
  #18
  #25
  TXD
  #12
  PCA9685
  ADDR
  A2
  A3

custom parts:
  Adafruit Thermocouple Amplifier MAX31855: Thermocouples are very sensitive, requiring a good amplifier with a cold-compensation reference. The MAX31855K does everything for you, and can be easily interfaced with any microcontroller, even one without an analog input. This breakout board has the chip itself, a 3.3V regulator with 10uF bypass capacitors and level shifting circuitry, all assembled and tested. Comes with a 2 pin terminal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
  Adafruit ADS1115 16Bit I2C ADC: For microcontrollers without an analog-to-digital converter or when you want a higher-precision ADC, the ADS1115 provides 16-bit precision at 860 samples/second over I2C. The chip can be configured as 4 single-ended input channels, or two differential channels. As a nice bonus, it even includes a programmable gain amplifier, up to x16, to help boost up smaller single/differential signals to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
  16-Channel 12-bit PWM Servo Driver - I2C: You want to make a cool robot, maybe a hexapod walker, or maybe just a piece of art with a lot of moving parts. Or maybe you want to drive a lot of LEDs with precise PWM output. Using only two pins, control 16 free-running PWM outputs! You can even chain up 62 breakouts to control up to 992 PWM outputs.
  Adafruit 4-channel I2C-safe Bi-directional Logic Level Converter: Because the Arduino (and Basic Stamp) are 5V devices, and most modern sensors, displays, flash cards and modes are 3.3V-only, many makers find that they need to perform level shifting/conversion to protect the 3.3V device from 5V. We do have some other handy level shifters in the shop, from the DIP 74LVC245 to the fancy bi-directional TXB0108. However, neither of these are happy to work with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
  2.1mm DC Barrel Jack: 2.1mm DC Barrel Jack with Thru-Hole Connectors (breadboardable)
