# Fritzing sketch main_board_prototype (saved by Fritzing 0.9.4)
breadboards: 1

parts:
  Part1 = Adafruit T-Cobbler Plus [part_number="Adafruit #1989 and #2028"]
  Part2 = Adafruit Thermocouple Amplifier MAX31855 [part_number="Adafruit #269"]
  Part3 = Adafruit ADS1115 16Bit I2C ADC [part_number="Adafruit #1085"]
  Part4 = Adafruit 4-channel I2C-safe Bi-directional Logic Level Converter [part_number="Adafruit #757"]
  R1 = Resistor [tolerance=±5% resistance=220 package="2512 [SMD]"]
  J1 = Camdenboss CTB0158-2 [part_number=CTB0158-2 package=THT]
  J2 = Camdenboss CTB0158-4 [part_number=CTB0158-4 package=THT]
  LED1 = LED - 3mm [color="Blue (470nm)" package="3 mm [THT]"]

nets:
  +3.3V: Part1.+3.3V, Part2.VIN, Part4.LV
  N1: Part1.SDA, Part4.A2
  N2: Part1.SCL, Part4.A1
  GND: Part1.GND, Part2.GND, Part3.GND, Part4.GND, R1.Pin_1, J1.pin2, J2.pin3
  N3: Part1.MISO, Part2.DO
  N4: Part1.SCLK, Part2.CLK
  N5: Part1.GPIO5, Part2.CS
  +5V: Part1.+5V, Part3.VDD, Part4.HV, J2.pin1
  N6: Part1.GPIO25, J1.pin1, LED1.cathode
  N7: Part3.AIN0, J2.pin2
  N8: Part3.SDA, Part4.B2
  N9: Part3.SCL, Part4.B1
  N10: R1.Pin_0, LED1.anode

custom parts:
  Adafruit T-Cobbler Plus: The Raspberry Pi has landed on the Maker World like a 40-GPIO pinned, quad-USB ported, credit card sized bomb of DIY joy. And while you can use most of our great Model B accessories by hooking up our downgrade cable, its probably a good time to upgrade your set up and accessorize using all of the 40 pins. That's why we now carry the Assembled Adafruit Pi T-Cobbler Plus - Breakout + Cable for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
  Adafruit Thermocouple Amplifier MAX31855: Thermocouples are very sensitive, requiring a good amplifier with a cold-compensation reference. The MAX31855K does everything for you, and can be easily interfaced with any microcontroller, even one without an analog input. This breakout board has the chip itself, a 3.3V regulator with 10uF bypass capacitors and level shifting circuitry, all assembled and tested. Comes with a 2 pin terminal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
  Adafruit ADS1115 16Bit I2C ADC: For microcontrollers without an analog-to-digital converter or when you want a higher-precision ADC, the ADS1115 provides 16-bit precision at 860 samples/second over I2C. The chip can be configured as 4 single-ended input channels, or two differential channels. As a nice bonus, it even includes a programmable gain amplifier, up to x16, to help boost up smaller single/differential signals to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
  Adafruit 4-channel I2C-safe Bi-directional Logic Level Converter: Because the Arduino (and Basic Stamp) are 5V devices, and most modern sensors, displays, flash cards and modes are 3.3V-only, many makers find that they need to perform level shifting/conversion to protect the 3.3V device from 5V. We do have some other handy level shifters in the shop, from the DIP 74LVC245 to the fancy bi-directional TXB0108. However, neither of these are happy to work with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
